// Logisim project DigitalDiceProject.circ as structural Verilog: 1 circuit, main circuit main
module main (
);

  wire [0:0] comparator_1_gt;
  wire [2:0] counter_1_q;

  Clock clock_1 ();  // open: out
  // AND_Gate and_1 has open pins: in0=comparator_1_gt[0], out=open
  Counter #(.width(3), .max('h6)) counter_1 (.Q(counter_1_q));  // open: load, D, count, carry, clk, clr
  Comparator #(.width(3)) comparator_1 (
    .a({2'b11, comparator_1_gt[0]}), .b(counter_1_q), .gt(comparator_1_gt[0]));  // open: eq, lt
  // Pins of 1 and 3 bits meet at {2'b11, comparator_1_gt[0]}
  // also tied to VCC on the sheet: comparator_1_gt[0]
endmodule
